// Digital circuit ALU_OVERTURE.dig as structural Verilog
module ALU_OVERTURE (
  input  [7:0] INSTRUCTION,
  input  [7:0] IN1,
  input  [7:0] IN2,
  output [7:0] OUT
);

  wire not_1_out;
  wire [7:0] add_1_s, and_2_out, nand_1_out, nor_1_out, or_1_out, sub_1_s;

  not not_1 (not_1_out, INSTRUCTION[7]);
  // And and_1 has open pins: In_1=INSTRUCTION[6], In_2=not_1_out, out=open
  assign or_1_out = IN1 | IN2;  // Or or_1, 8 bits wide
  assign nand_1_out = ~(IN1 & IN2);  // NAnd nand_1, 8 bits wide
  assign nor_1_out = ~(IN1 | IN2);  // NOr nor_1, 8 bits wide
  assign and_2_out = IN1 & IN2;  // And and_2, 8 bits wide
  Add #(.Bits(8)) add_1 (.a(IN1), .b(IN2), .c_i(1'b0), .s(add_1_s));  // open: c_o
  Sub #(.Bits(8)) sub_1 (.a(IN1), .b(IN2), .c_i(1'b0), .s(sub_1_s));  // open: c_o
  Multiplexer #(.Bits(8), .Selector_Bits(3)) multiplexer_1 (
    .sel(INSTRUCTION[2:0]), .in_0(or_1_out), .in_1(nand_1_out), .in_2(nor_1_out), .in_3(and_2_out),
    .in_4(add_1_s), .in_5(sub_1_s), .in_6({8{1'b0}}), .in_7({8{1'b0}}), .out(OUT));

  // Notes on the sheet:
  //   OR
  //   NAND
  //   NOR
  //   AND
  //   ADD
  //   SUB
endmodule
